// Logisim project t_flip_flop.circ as structural Verilog: 1 circuit, main circuit main
module main (
  input  data,
  input  reset,
  input  set,
  input  we,
  input  data_2,
  input  clk,
  input  x,
  input  y,
  input  toggle,
  input  clk_2
);

  wire nand_1_out, nand_2_out, nand_3_out, nand_4_out, nand_5_out, nand_6_out, nand_7_out, nand_8_out,
       nand_9_out, nand_10_out, nand_11_out, nand_12_out, nand_13_out, nand_14_out, nand_15_out, nand_16_out,
       nand_17_out, nand_18_out, nor_1_out, nor_2_out, nor_3_out, nor_4_out, nor_5_out, nor_6_out, nor_7_out,
       nor_8_out, nor_9_out, nor_10_out, nor_11_out, nor_12_out, not_1_out, not_2_out, not_3_out, not_4_out,
       not_5_out, not_6_out, not_7_out, not_8_out, not_9_out, not_10_out, not_11_out, not_12_out, not_13_out,
       not_14_out, not_15_out, not_16_out, not_17_out;

  nand nand_1 (nand_1_out, nor_11_out, nand_2_out);
  nand nand_2 (nand_2_out, nor_11_out, toggle);
  nand nand_3 (nand_3_out, nand_2_out, toggle);
  nor nor_1 (nor_1_out, reset, nor_2_out);
  nor nor_2 (nor_2_out, nor_1_out, set);
  not not_1 (not_1_out, data_2);
  not not_2 (not_2_out, clk);
  nand nand_4 (nand_4_out, nand_1_out, nand_3_out);
  // Probe on nor_1_out
  // Probe on nor_2_out
  nand nand_5 (nand_5_out, not_1_out, not_2_out);
  nand nand_6 (nand_6_out, data_2, not_2_out);
  not not_3 (not_3_out, nand_4_out);
  not not_4 (not_4_out, clk_2);
  not not_5 (not_5_out, nand_5_out);
  not not_6 (not_6_out, nand_6_out);
  nand nand_7 (nand_7_out, not_3_out, not_4_out);
  nand nand_8 (nand_8_out, nand_4_out, not_4_out);
  nor nor_3 (nor_3_out, not_5_out, nor_4_out);
  nor nor_4 (nor_4_out, nor_3_out, not_6_out);
  not not_7 (not_7_out, nand_7_out);
  not not_8 (not_8_out, nand_8_out);
  not not_9 (not_9_out, data);
  nor nor_5 (nor_5_out, not_7_out, nor_6_out);
  nor nor_6 (nor_6_out, nor_5_out, not_8_out);
  not not_10 (not_10_out, nand_9_out);
  nand nand_9 (nand_9_out, not_9_out, we);
  nand nand_10 (nand_10_out, data, we);
  not not_11 (not_11_out, nand_10_out);
  not not_12 (not_12_out, nor_3_out);
  nor nor_7 (nor_7_out, not_10_out, nor_8_out);
  nor nor_8 (nor_8_out, nor_7_out, not_11_out);
  not not_13 (not_13_out, nand_11_out);
  nand nand_11 (nand_11_out, not_12_out, clk);
  nand nand_12 (nand_12_out, nor_3_out, clk);
  not not_14 (not_14_out, nand_12_out);
  nand nand_13 (nand_13_out, x, y);
  not not_15 (not_15_out, nor_5_out);
  // Probe on nor_7_out
  // Probe on nor_8_out
  nor nor_9 (nor_9_out, not_13_out, nor_10_out);
  nor nor_10 (nor_10_out, nor_9_out, not_14_out);
  nand nand_14 (nand_14_out, x, nand_13_out);
  nand nand_15 (nand_15_out, nand_14_out, nand_16_out);
  nand nand_16 (nand_16_out, nand_13_out, y);
  nand nand_17 (nand_17_out, not_15_out, clk_2);
  not not_16 (not_16_out, nand_17_out);
  not not_17 (not_17_out, nand_18_out);
  nand nand_18 (nand_18_out, nor_5_out, clk_2);
  // Probe on nor_9_out
  // Probe on nor_10_out
  // Probe on nand_15_out
  nor nor_11 (nor_11_out, not_16_out, nor_12_out);
  nor nor_12 (nor_12_out, nor_11_out, not_17_out);
  // Probe on nor_11_out
  // Probe on nor_12_out

  // Notes on the sheet:
  //   XOR
  //   SR-Latch
  //   D-Latch
  //   Попов Владимир Сергеевич
  //   T-Flip-Flop
  //   D-Flip-Flop
  //   D-Flip-Flop
  //   D-Latch
  //   SR-Latch
  //   D-Latch
  //   XOR
endmodule
